// Logisim project Traballho_AV1.circ as structural Verilog: 9 circuits, main circuit main
module main (
  input  A,
  input  B,
  input  C
);

  wire conjunto_a_1_s, conjunto_b_1_s, conjunto_c_1_s, conjunto_d_1_s, conjunto_e_1_s, conjunto_f_1_s,
       conjunto_g_1_s;

  conjunto_a conjunto_a_1 (.A(A), .B(B), .C(C), .S(conjunto_a_1_s));
  conjunto_b conjunto_b_1 (.A(A), .B(B), .C(C), .S(conjunto_b_1_s));
  conjunto_c conjunto_c_1 (.A(A), .B(B), .C(C), .S(conjunto_c_1_s));
  conjunto_d conjunto_d_1 (.A(A), .B(B), .C(C), .S(conjunto_d_1_s));
  conjunto_e conjunto_e_1 (.A(A), .B(B), .C(C), .S(conjunto_e_1_s));
  conjunto_f conjunto_f_1 (.A(A), .B(B), .C(C), .S(conjunto_f_1_s));
  conjunto_g conjunto_g_1 (.A(A), .B(B), .C(C), .S(conjunto_g_1_s));
  _7_Segment_Display u_7_segment_display_1 (
    .g(conjunto_g_1_s), .f(conjunto_f_1_s), .a(conjunto_a_1_s), .b(conjunto_b_1_s), .e(conjunto_e_1_s),
    .d(conjunto_d_1_s), .c(conjunto_c_1_s));  // open: dp
endmodule

module conjunto_a (
  input  A,
  input  B,
  input  C,
  output S
);

  wire and_1_out, and_2_out, not_1_out, not_2_out;

  not not_1 (not_1_out, A);
  not not_2 (not_2_out, C);
  and and_1 (and_1_out, C, A);
  and and_2 (and_2_out, not_1_out, not_2_out);
  or or_1 (S, and_2_out, B, and_1_out);
endmodule

module conjunto_b (
  input  A,
  input  B,
  input  C,
  output S
);

  wire and_1_out, and_2_out, not_1_out, not_2_out, not_3_out;

  not not_1 (not_1_out, B);
  not not_2 (not_2_out, C);
  and and_1 (and_1_out, not_1_out, not_2_out);
  and and_2 (and_2_out, B, C);
  not not_3 (not_3_out, A);
  or or_1 (S, and_1_out, not_3_out, and_2_out);
endmodule

module conjunto_c (
  input  A,
  input  B,
  input  C,
  output S
);

  wire not_1_out;

  not not_1 (not_1_out, B);
  or or_1 (S, A, not_1_out, C);
endmodule

module conjunto_d (
  input  A,
  input  B,
  input  C,
  output S
);

  wire and_1_out, and_2_out, and_3_out, and_4_out, not_1_out, not_2_out, not_3_out;

  not not_1 (not_1_out, A);
  not not_2 (not_2_out, B);
  not not_3 (not_3_out, C);
  and and_1 (and_1_out, not_1_out, not_3_out);
  and and_2 (and_2_out, A, not_2_out, C);
  and and_3 (and_3_out, B, not_3_out);
  and and_4 (and_4_out, B, not_1_out);
  or or_1 (S, and_1_out, and_2_out, and_3_out, and_4_out);
endmodule

module conjunto_e (
  input  A,
  input  B,
  input  C,
  output S
);

  wire and_1_out, and_2_out, not_1_out, not_2_out;

  not not_1 (not_1_out, A);
  not not_2 (not_2_out, C);
  and and_1 (and_1_out, not_1_out, not_2_out);
  or or_1 (S, and_1_out, and_2_out);
  and and_2 (and_2_out, B, not_2_out);
endmodule

module conjunto_f (
  input  A,
  input  B,
  input  C,
  output S
);

  wire and_1_out, and_2_out, and_3_out, not_1_out, not_2_out;

  not not_1 (not_1_out, B);
  not not_2 (not_2_out, C);
  and and_1 (and_1_out, not_1_out, not_2_out);
  and and_2 (and_2_out, A, not_1_out);
  and and_3 (and_3_out, A, not_2_out);
  or or_1 (S, and_1_out, and_2_out, and_3_out);
endmodule

module conjunto_g (
  input  A,
  input  B,
  input  C,
  output S
);

  wire and_1_out, and_2_out, and_3_out, not_1_out, not_2_out, not_3_out;

  not not_1 (not_1_out, A);
  not not_2 (not_2_out, B);
  not not_3 (not_3_out, C);
  and and_1 (and_1_out, not_1_out, B);
  and and_2 (and_2_out, A, not_2_out);
  and and_3 (and_3_out, A, not_3_out);
  or or_1 (S, and_1_out, and_2_out, and_3_out);
endmodule

module conjuntos (
  input  A0,
  input  B0,
  input  C0,
  output a,
  output b,
  output c,
  output d,
  output e,
  output f,
  output g
);

  wire and_1_out, and_2_out, and_3_out, and_4_out, and_5_out, and_6_out, and_7_out, and_8_out, and_9_out,
       and_10_out, and_11_out, and_12_out, and_13_out, and_14_out, and_15_out, and_16_out, not_1_out,
       not_2_out, not_3_out;

  not not_1 (not_1_out, A0);
  not not_2 (not_2_out, B0);
  not not_3 (not_3_out, C0);
  and and_1 (and_1_out, not_1_out, not_3_out);
  and and_2 (and_2_out, A0, C0);
  and and_3 (and_3_out, not_2_out, not_3_out);
  and and_4 (and_4_out, B0, C0);
  or or_1 (c, not_2_out, C0, A0);
  and and_5 (and_5_out, not_1_out, not_3_out);
  and and_6 (and_6_out, not_1_out, B0);
  and and_7 (and_7_out, B0, not_3_out);
  and and_8 (and_8_out, A0, not_2_out, C0);
  and and_9 (and_9_out, not_1_out, not_3_out);
  and and_10 (and_10_out, B0, not_3_out);
  and and_11 (and_11_out, not_2_out, not_3_out);
  and and_12 (and_12_out, A0, not_2_out);
  and and_13 (and_13_out, A0, not_3_out);
  and and_14 (and_14_out, not_1_out, B0);
  and and_15 (and_15_out, A0, not_2_out);
  and and_16 (and_16_out, A0, not_3_out);
  or or_2 (a, and_1_out, B0, and_2_out);
  or or_3 (b, not_1_out, and_3_out, and_4_out);
  or or_4 (d, and_5_out, and_6_out, and_7_out, and_8_out);
  or or_5 (e, and_9_out, and_10_out);
  or or_6 (f, and_11_out, and_12_out, and_13_out);
  or or_7 (g, and_14_out, and_15_out, and_16_out);
endmodule
